// Logisim project carte 1.circ as structural Verilog: 1 circuit, main circuit main
module main (
  input  in_1,
  input  in_2,
  input  in_3,
  input  in_4,
  output out_5,
  output out_6,
  output out_7,
  output out_8
);

  wire and_1_out, and_2_out, or_1_out, or_2_out;

  and and_1 (and_1_out, in_1, in_3);
  and and_2 (and_2_out, in_1, in_3, in_4);
  or or_1 (or_1_out, and_1_out, and_2_out);
  or or_2 (or_2_out, and_1_out, and_2_out);
  xor xor_1 (out_5, in_2, or_1_out);
  xor xor_2 (out_7, in_2, or_2_out);
  xor xor_3 (out_8, in_2, and_2_out);
endmodule
