// Logisim project carte 2.circ as structural Verilog: 1 circuit, main circuit main
module main (
  input  in_1,
  input  in_2,
  input  in_3,
  input  in_4,
  output out_5,
  output out_6,
  output out_7,
  output out_8
);

  wire not_1_out, or_1_out;

  or or_1 (or_1_out, in_1, in_2, in_3);
  not not_1 (not_1_out, or_1_out);
  and and_1 (out_8, not_1_out, in_4);
endmodule
