// Logisim project carte 3.circ as structural Verilog: 1 circuit, main circuit main
module main (
  input  in_1,
  input  in_2,
  input  in_3,
  input  in_4,
  output out_5,
  output out_6,
  output out_7,
  output out_8
);

  wire and_1_out, and_2_out, and_3_out;

  and and_1 (and_1_out, in_2, in_3, in_4);
  and and_2 (and_2_out, in_1, in_2, in_4);
  and and_3 (and_3_out, in_1, in_2, in_3);
  xor xor_1 (out_5, and_2_out, and_3_out);
  ExactlyOne xor_2 (.out(out_6), .in0(and_1_out), .in2(and_2_out), .in4(and_3_out));
  xor xor_3 (out_7, and_1_out, and_3_out);
  xor xor_4 (out_8, and_1_out, and_2_out);
endmodule
