// Logisim project carte 4.circ as structural Verilog: 1 circuit, main circuit main
module main (
  input  in_1,
  input  in_2,
  input  in_3,
  input  in_4,
  output out_5,
  output out_6,
  output out_7,
  output out_8
);

  wire or_1_out, or_2_out;

  or or_1 (or_1_out, in_2, in_3, in_4);
  or or_2 (or_2_out, in_1, in_3, in_4);
  ExactlyOne xor_1 (.out(out_5), .in0(in_4), .in1(in_1), .in2(in_3), .in3(or_1_out), .in4(in_2));
  ExactlyOne xor_2 (.out(out_6), .in0(in_3), .in1(in_2), .in2(in_1), .in3(or_2_out), .in4(in_4));
endmodule
