// Logisim project carte 5.circ as structural Verilog: 1 circuit, main circuit main
module main (
  input  in_1,
  input  in_2,
  input  in_3,
  input  in_4,
  output out_5,
  output out_6,
  output out_7,
  output out_8
);

  wire and_1_out, nor_1_out;

  and and_1 (and_1_out, in_1, in_4);
  nor nor_1 (nor_1_out, in_2, in_3);
  and and_2 (out_5, and_1_out, nor_1_out);

  assign out_8 = out_5;
endmodule
