// Logisim project circuit logique coffre fort.circ as structural Verilog: 1 circuit, main circuit main
module main (
  input  in_1,
  input  in_2,
  input  in_3,
  input  in_4,
  output out_5,
  output out_6,
  output out_7,
  output out_8,
  output out_9,
  output out_10,
  output out_11,
  output out_12
);

  wire and_1_out, and_2_out, and_3_out, and_4_out, and_5_out, and_6_out, and_7_out, and_8_out, and_9_out,
       and_10_out, and_11_out, and_12_out, and_13_out, and_14_out, and_15_out, and_16_out, and_17_out,
       and_18_out, and_19_out, and_20_out, nor_1_out, not_1_out, not_2_out, not_3_out, not_4_out, not_5_out,
       not_6_out, xor_1_out, xor_2_out, xor_3_out, xor_8_out, xor_10_out;

  and and_1 (and_1_out, in_1, in_3);
  and and_2 (and_2_out, in_3, in_1, in_4);
  ExactlyOne xor_1 (.out(xor_1_out), .in1(in_1), .in2(in_2), .in3(in_3));
  and and_3 (and_3_out, in_1, in_2);
  and and_4 (and_4_out, in_1, in_3);
  and and_5 (and_5_out, in_2, in_3);
  and and_6 (and_6_out, in_1, in_3, in_4);
  and and_7 (and_7_out, in_4, in_2, in_1);
  and and_8 (and_8_out, in_1, in_2, in_3);
  nor nor_1 (nor_1_out, in_1, in_2, in_3, in_4);
  and and_9 (and_9_out, in_1, in_4);
  xor xor_2 (xor_2_out, in_2, in_3);
  and and_10 (and_10_out, in_2, in_3);
  and and_11 (and_11_out, in_1, in_2, in_3, in_4);
  and and_12 (and_12_out, in_1, in_2);
  and and_13 (and_13_out, in_1, in_2, in_4);
  and and_14 (and_14_out, in_3, in_4);
  and and_15 (and_15_out, in_1, in_3);
  and and_16 (and_16_out, in_2, in_3);
  and and_17 (and_17_out, in_1, in_3, in_4);
  and and_18 (and_18_out, in_2, in_3, in_4);
  and and_19 (and_19_out, in_2, in_4);
  and and_20 (and_20_out, in_2, in_3, in_3);
  and and_21 (out_12, in_3, in_3, in_4);
  not not_1 (not_1_out, xor_1_out);
  not not_2 (not_2_out, and_3_out);
  not not_3 (not_3_out, and_4_out);
  not not_4 (not_4_out, and_5_out);
  not not_5 (not_5_out, xor_2_out);
  not not_6 (not_6_out, and_10_out);
  ExactlyOne xor_3 (.out(xor_3_out), .in0(and_13_out), .in1(and_14_out), .in3(and_15_out), .in4(and_16_out));
  xor xor_4 (out_5, and_1_out, and_2_out);
  and and_22 (out_6, not_1_out, in_4, not_2_out, not_3_out, not_4_out);
  ExactlyOne xor_5 (.out(out_7), .in1(and_6_out), .in2(and_7_out), .in3(and_8_out));
  ExactlyOne xor_6 (.out(out_8), .in0(nor_1_out), .in2(in_1), .in4(in_2));
  and and_23 (out_9, and_9_out, not_5_out, not_6_out);
  xor xor_7 (out_10, and_11_out, xor_8_out);
  ExactlyOne xor_8 (.out(xor_8_out), .in1(in_3), .in3(and_12_out), .in4(xor_10_out));
  xor xor_9 (out_11, and_19_out, and_20_out);
  ExactlyOne xor_10 (.out(xor_10_out), .in0(xor_3_out), .in2(and_17_out), .in4(and_18_out));
endmodule
